# Fritzing sketch Breadboard (saved by Fritzing 0.9.4)
breadboards: 1

parts:
  SparkFun_RedBoard_Artemis_ATP1 = SparkFun RedBoard Artemis ATP
  S2 = Pushbutton [package="[THT]"]
  S3 = Pushbutton [package="[THT]"]
  R1 = Resistor [tolerance=±5% resistance=10k package=THT]
  R2 = Resistor [tolerance=±5% resistance=10k package=THT]
  R3 = Resistor [tolerance=±5% resistance=10k package=THT]
  S1 = Pushbutton [package="[THT]"]
  LED2 = LED - 3mm [color="Green (555nm)" package="3 mm [THT]"]
  LED3 = LED - 3mm [color="Red (633nm)" package="3 mm [THT]"]
  LED4 = LED - 3mm [color="Blue (430nm)" package="3 mm [THT]"]
  R4 = Resistor [tolerance=±5% resistance=470 package=THT]
  R5 = Resistor [tolerance=±5% resistance=470 package=THT]
  R6 = Resistor [tolerance=±5% resistance=470 package=THT]

nets:
  N1: SparkFun_RedBoard_Artemis_ATP1.GND, S3.Pin_1, S3.Pin_2, R1.Pin_0, R2.Pin_0, R3.Pin_0, R4.Pin_0, R5.Pin_0, R6.Pin_0
  N2: SparkFun_RedBoard_Artemis_ATP1.VDD, S2.Pin_1, S2.Pin_2, S1.Pin_1, S1.Pin_2
  N3: SparkFun_RedBoard_Artemis_ATP1.~D18, LED2.anode
  N4: SparkFun_RedBoard_Artemis_ATP1.~D19, LED4.anode
  N5: SparkFun_RedBoard_Artemis_ATP1.D17, LED3.anode
  N6: SparkFun_RedBoard_Artemis_ATP1.D2, R3.Pin_1, S1.Pin_3, S1.Pin_4
  N7: SparkFun_RedBoard_Artemis_ATP1.D1, S2.Pin_3, S2.Pin_4, R2.Pin_1
  N8: SparkFun_RedBoard_Artemis_ATP1.D0, S3.Pin_3, S3.Pin_4, R1.Pin_1
  N9: LED2.cathode, R5.Pin_1
  N10: LED3.cathode, R4.Pin_1
  N11: LED4.cathode, R6.Pin_1

custom parts:
  SparkFun RedBoard Artemis ATP: The RedBoard Artemis ATP is affectionately called 'All the Pins!' at SparkFun. The Artemis module has 48 GPIO and this board breaks out absolutely every one of them in a familiar Mega like form factor. What's with the silkscreen labels? They're all over the place. We decided to label the pins as they are assigned on the Apollo3 IC itself. This makes finding the pin with the function you desire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
